# Fritzing sketch mcp9808 (saved by Fritzing 0.9.2b)
breadboards: 1

parts:
  Composant1 = Arduino Leonardo (Rev3b)
  Part6 = MCP9808

nets:
  3V3: Composant1.3V3, Part6.VCC
  GND: Composant1.GND, Part6.GND
  N1: Composant1.SDA, Part6.SDA
  N2: Composant1.SCL, Part6.SCL
