# Fritzing sketch esp8266-mcp9808 (saved by Fritzing 0.9.2b)

parts:
  Part7 = MCP9808
  U1 = NodeMCU V1.0

nets:
  N1: Part7.SDA, U1.D2
  N2: Part7.SCL, U1.D1
  VCC: Part7.VCC, U1.3V3
  GND: Part7.GND, U1.GND

custom parts:
  NodeMCU V1.0: ESP9266 based NodeMCU
